// Digital circuit Contador.dig as structural Verilog
module Contador (
  input  clk,
  input  [15:0] in_7,
  output [3:0] out_1,
  output [3:0] out_2,
  output [3:0] out_3,
  output [3:0] out_4,
  output [3:0] out_5
);

  wire and_1_out, and_2_out, and_3_out, and_5_out, and_6_out, and_7_out, and_8_out, and_9_out,
       comparator_1_eq, comparator_2_eq, comparator_3_eq, comparator_4_eq, comparator_5_eq, not_1_out,
       not_2_out, not_3_out, not_4_out, not_5_out, or_1_out, or_2_out, or_3_out, or_4_out, reloj;
  wire [15:0] c, d, div_1_q, div_2_q, div_3_q, div_4_q, m, mm, u;

  Comparator #(.Bits(4)) comparator_1 (.a(out_5), .b(mm[3:0]), .eq(comparator_1_eq));  // open: gt, lt
  Div #(.Bits(16)) div_1 (.a(in_7), .b(16'ha), .q(div_1_q), .r(u));
  Counter #(.Bits(4)) counter_1 (.en(1'b1), .C(and_2_out), .clr(and_1_out), .out(out_5));  // open: ovf
  and and_1 (and_1_out, out_5[0], out_5[3]);
  not not_1 (not_1_out, comparator_1_eq);
  Div #(.Bits(16)) div_2 (.a(div_1_q), .b(16'ha), .q(div_2_q), .r(d));
  Comparator #(.Bits(4)) comparator_2 (.a(out_4), .b(m[3:0]), .eq(comparator_2_eq));  // open: gt, lt
  Counter #(.Bits(4)) counter_2 (.en(1'b1), .C(and_3_out), .clr(and_2_out), .out(out_4));  // open: ovf
  and and_2 (and_2_out, out_4[0], out_4[3]);
  not not_2 (not_2_out, comparator_2_eq);
  Div #(.Bits(16)) div_3 (.a(div_2_q), .b(16'ha), .q(div_3_q), .r(c));
  or or_1 (or_1_out, or_2_out, not_1_out);
  Counter #(.Bits(4)) counter_3 (.en(1'b1), .C(and_5_out), .clr(and_3_out), .out(out_3));  // open: ovf
  and and_3 (and_3_out, out_3[0], out_3[3]);
  Comparator #(.Bits(4)) comparator_3 (.a(out_3), .b(c[3:0]), .eq(comparator_3_eq));  // open: gt, lt
  Div #(.Bits(16)) div_4 (.a(div_3_q), .b(16'ha), .q(div_4_q), .r(m));
  not not_3 (not_3_out, comparator_3_eq);
  or or_2 (or_2_out, or_3_out, not_2_out);
  and and_4 (reloj, or_1_out, clk);
  Div #(.Bits(16)) div_5 (.a(div_4_q), .b(16'ha), .r(mm));  // open: q
  Counter #(.Bits(4)) counter_4 (.en(1'b1), .C(and_7_out), .clr(and_5_out), .out(out_2));  // open: ovf
  and and_5 (and_5_out, out_2[0], out_2[3]);
  Comparator #(.Bits(4)) comparator_4 (.a(out_2), .b(d[3:0]), .eq(comparator_4_eq));  // open: gt, lt
  not not_4 (not_4_out, comparator_4_eq);
  or or_3 (or_3_out, or_4_out, not_3_out);
  and and_6 (and_6_out, not_5_out, not_4_out);
  Counter #(.Bits(4)) counter_5 (.en(1'b1), .C(reloj), .clr(and_7_out), .out(out_1));  // open: ovf
  and and_7 (and_7_out, out_1[0], out_1[3]);
  or or_4 (or_4_out, and_9_out, and_8_out, and_6_out);
  Comparator #(.Bits(4)) comparator_5 (.a(out_1), .b(u[3:0]), .eq(comparator_5_eq));  // open: gt, lt
  not not_5 (not_5_out, comparator_5_eq);
  and and_8 (and_8_out, not_5_out, comparator_4_eq);
  and and_9 (and_9_out, comparator_5_eq, not_4_out);

  // Notes on the sheet:
  //   clk: Hz: 2000
  //   in_7: default 14515
endmodule
